# Fritzing sketch uolli (saved by Fritzing 0.9.3b)

parts:
  U1 = ESP8266 WiFi Module [part_number=ESP8266]
  U2 = L298_BRIDGE_DRIVER [package=powerso20]
  BAT1 = 18650 battery holder [package=battery-18650-kit]
  BAT2 = 18650 battery holder [package=battery-18650-kit]
  M1 = DC Motor
  M2 = DC Motor
  M3 = DC Motor
  M4 = DC Motor
  Componente1 = Arduino Mega 2560 (Rev3)
  J1 = Basic Servo
  HCSR04 = SRF05 Ultrasonic Rangefinder
  PIR1 = PIR sensor
  PIR2 = PIR sensor
  PIR3 = PIR sensor
  PIR4 = PIR sensor
  PIR5 = PIR sensor
  R1 = Resistor [tolerance=±5% resistance=150 package=THT]
  R2 = Resistor [tolerance=±5% resistance=150 package=THT]
  R3 = Resistor [tolerance=±5% resistance=150 package=THT]
  R4 = Resistor [tolerance=±5% resistance=150 package=THT]
  R5 = Resistor [tolerance=±5% resistance=150 package=THT]
  S1 = Momentary Switch [package=ksa_sealed_tac_switch]
  LED2 = smd LED [color="Red (633nm)" package="0603 [SMD]"]
  LED1 = smd LED [color="Red (633nm)" package="0603 [SMD]"]
  LED3 = smd LED [color="Red (633nm)" package="0603 [SMD]"]
  LED4 = smd LED [color="Red (633nm)" package="0603 [SMD]"]
  LED5 = smd LED [color="Red (633nm)" package="0603 [SMD]"]
  R6 = Resistor [tolerance=±5% resistance=150 package=THT]
  IR1 = TSOP312.., 314.. [part_number=1838B package=THT]
  Part1 = KY-012 Active Buzzer Module [package="Breakout board"]

nets:
  N1: U1.RXD, Componente1.D18/TX1
  VCC: U1.VCC, Componente1.3V3
  GND: U1.GND, U2.GND, BAT2.-, M1.pin_2, M2.pin_2, M3.pin_2, M4.pin_2, Componente1.GND, J1.gnd, HCSR04.GND, PIR1.GND, PIR2.GND, PIR3.GND, PIR4.GND, PIR5.GND, S1.4, LED2.cathode, LED1.cathode, LED3.cathode, LED4.cathode, LED5.cathode, IR1.GND, Part1.GND
  N2: U1.TXD, Componente1.D19/RX1
  N3: U2.OUT1, M3.pin_1
  N4: U2.OUT2, M1.pin_1
  N5: U2.VS, BAT1.+, Componente1.VIN
  N6: U2.IN1, Componente1.D22
  N7: U2.ENA, Componente1.D2_PWM
  N8: U2.IN2, Componente1.D23
  VDD: U2.VSS, Componente1.5V, J1.vcc, HCSR04.VCC, PIR1.VDD, PIR2.VDD, PIR3.VDD, PIR4.VDD, PIR5.VDD, IR1.Vs, Part1.VCC
  N9: U2.IN3, Componente1.D24
  N10: U2.ENB, Componente1.D3_PWM
  N11: U2.IN4, Componente1.D25
  N12: U2.OUT3, M2.pin_1
  N13: U2.OUT4, M4.pin_1
  N14: BAT1.-, BAT2.+
  N15: Componente1.D11_PWM, HCSR04.Echo
  N16: Componente1.D10_PWM, HCSR04.Trig
  N17: Componente1.D4_PWM, J1.pulse
  N18: Componente1.D5_PWM, IR1.Data
  N19: Componente1.D6_PWM, Part1.SIG
  N20: Componente1.D28, PIR1.SIG
  N21: Componente1.D29, PIR2.SIG
  N22: Componente1.D30, PIR3.SIG
  N23: Componente1.D31, PIR4.SIG
  N24: Componente1.D32, PIR5.SIG
  N25: Componente1.D33, R6.Pin_0
  N26: Componente1.D34, R1.Pin_0
  N27: Componente1.D35, R2.Pin_0
  N28: Componente1.D36, R3.Pin_0
  N29: Componente1.D37, R4.Pin_0
  N30: Componente1.D38, R5.Pin_0
  N31: R1.Pin_1, LED1.anode
  N32: R2.Pin_1, LED2.anode
  N33: R3.Pin_1, LED3.anode
  N34: R4.Pin_1, LED4.anode
  N35: R5.Pin_1, LED5.anode
  N36: S1.1, R6.Pin_1

custom parts:
  L298_BRIDGE_DRIVER: Full-bridge power driver IC
  18650 battery holder: 18650 Battery Holder
  KY-012 Active Buzzer Module: Active Piezoelectric Buzzer Module Keyes KY-012, it produces single-tone sound when signal is high.
